// Logisim project hw4-8.circ as structural Verilog: 1 circuit, main circuit main
module main (
  input  [3:0] A,
  input  [3:0] B,
  input  Top,
  input  Bottom,
  input  Sub,
  output [3:0] Out
);

  wire [3:0] multiplexer_1_out, multiplexer_2_out, xor_1_out;

  Multiplexer #(.width(4), .enable("false")) multiplexer_1 (.in0(A), .in1(B), .out(multiplexer_1_out), .sel(Top));
  Multiplexer #(.width(4), .enable("false")) multiplexer_2 (.in0(A), .in1(B), .out(multiplexer_2_out), .sel(Bottom));
  assign xor_1_out = multiplexer_2_out ^ {4{Sub}};  // XOR_Gate xor_1, 4 bits wide
  Adder #(.width(4)) adder_1 (.a(multiplexer_1_out), .b(xor_1_out), .out(Out), .cin(Sub));  // open: cout

  // Notes on the sheet:
  //   4bit Controlled Adder Subtractor
endmodule
