// Logisim project lab3-multiplexers-2.circ as structural Verilog: 1 circuit, main circuit main
module main (
  input  [3:0] A,
  input  [3:0] B,
  input  Right,
  output [3:0] out_4
);

  Multiplexer #(.width(4), .disabled(0), .enable("false")) multiplexer_1 (.in0(A), .in1(B), .out(out_4), .sel(Right));
endmodule
