// Logisim project lab4-2-1.circ as structural Verilog: 1 circuit, main circuit main
module main (
  input  [4:0] A,
  input  [4:0] B,
  input  [4:0] C,
  input  [4:0] D,
  input  [1:0] Demux,
  input  [1:0] Rmux,
  input  Sub,
  output [4:0] Sum
);

  wire [4:0] multiplexer_1_out, multiplexer_2_out, xor_1_out;

  Multiplexer #(.select(2), .width(5), .enable("false")) multiplexer_1 (
    .in0(A), .in1(B), .in2(C), .in3(D), .out(multiplexer_1_out), .sel(Demux));
  Multiplexer #(.select(2), .width(5), .enable("false")) multiplexer_2 (
    .in0(A), .in1(B), .in2(C), .in3(D), .out(multiplexer_2_out), .sel(Rmux));
  assign xor_1_out = multiplexer_2_out ^ {5{Sub}};  // XOR_Gate xor_1, 5 bits wide
  Adder #(.width(5)) adder_1 (.a(multiplexer_1_out), .b(xor_1_out), .out(Sum), .cin(Sub));  // open: cout

  // Notes on the sheet:
  //   Two-Port Adder
endmodule
