// Logisim project lab3-alu-1.circ as structural Verilog: 1 circuit, main circuit main
module main (
  input  [1:0] Control,
  input  [3:0] A,
  output [3:0] Output
);

  wire and_1_out, and_2_out, and_3_out, xor_1_out, xor_2_out, xor_3_out, xor_4_out;

  xor xor_1 (xor_1_out, A[0], Control[1]);
  xor xor_2 (xor_2_out, A[1], Control[1]);
  xor xor_3 (xor_3_out, A[2], Control[1]);
  xor xor_4 (xor_4_out, A[3], Control[1]);
  and and_1 (and_1_out, xor_1_out, Control[0]);
  and and_2 (and_2_out, xor_2_out, and_1_out);
  and and_3 (and_3_out, xor_3_out, and_2_out);
  // AND_Gate and_4 has open pins: in0=xor_4_out, in1=and_3_out, out=open
  xor xor_5 (Output[0], Control[0], xor_1_out);
  xor xor_6 (Output[1], and_1_out, xor_2_out);
  xor xor_7 (Output[2], and_2_out, xor_3_out);
  xor xor_8 (Output[3], and_3_out, xor_4_out);

  // Notes on the sheet:
  //   Inverter
  //   ALU Unit
  //   Incrementer
endmodule
