// Logisim project lab3-decoders-1.circ as structural Verilog: 1 circuit, main circuit main
module main (
  input  [2:0] in_1,
  output out_2,
  output out_3,
  output out_4,
  output out_5,
  output out_6,
  output out_7,
  output out_8,
  output out_9
);

  wire not_1_out, not_2_out, not_3_out;

  not not_1 (not_1_out, in_1[2]);
  not not_2 (not_2_out, in_1[1]);
  not not_3 (not_3_out, in_1[0]);
  and and_1 (out_2, not_1_out, not_2_out, not_3_out);
  and and_2 (out_3, not_1_out, not_2_out, in_1[0]);
  and and_3 (out_4, not_1_out, in_1[1], not_3_out);
  and and_4 (out_5, not_1_out, in_1[1], in_1[0]);
  and and_5 (out_6, in_1[2], not_2_out, not_3_out);
  and and_6 (out_7, in_1[2], not_2_out, in_1[0]);
  and and_7 (out_8, in_1[2], in_1[1], not_3_out);
  and and_8 (out_9, in_1[2], in_1[1], in_1[0]);
endmodule
