// Logisim project lab3-multiplexers-1.circ as structural Verilog: 1 circuit, main circuit main
module main (
  input  Right,
  input  [3:0] A,
  input  [3:0] B,
  output out_4,
  output out_5,
  output out_6,
  output out_7
);

  wire and_1_out, and_2_out, and_3_out, and_4_out, and_5_out, and_6_out, and_7_out, and_8_out, not_1_out;

  not not_1 (not_1_out, Right);
  and and_1 (and_1_out, not_1_out, A[3]);
  and and_2 (and_2_out, not_1_out, A[0]);
  and and_3 (and_3_out, not_1_out, A[2]);
  and and_4 (and_4_out, not_1_out, A[1]);
  or or_1 (out_4, and_1_out, and_5_out);
  or or_2 (out_6, and_4_out, and_6_out);
  or or_3 (out_5, and_3_out, and_7_out);
  and and_5 (and_5_out, Right, B[3]);
  and and_6 (and_6_out, Right, B[1]);
  and and_7 (and_7_out, Right, B[2]);
  or or_4 (out_7, and_2_out, and_8_out);
  and and_8 (and_8_out, Right, B[0]);
endmodule
