// Logisim project lab4-1-5.circ as structural Verilog: 1 circuit, main circuit main
module main (
  input  Sub,
  input  in_2,
  input  [3:0] A,
  input  B,
  input  [3:0] in_5,
  output out_6,
  output [3:0] out_7,
  output Overflow
);

  wire and_1_out, and_2_out, and_3_out, and_4_out, and_5_out, and_6_out, and_7_out, and_8_out, not_1_out,
       not_2_out, not_3_out, not_4_out, not_5_out, not_6_out;
  wire [4:0] xor_1_out;

  xor xor_1 (xor_1_out[0], in_5[0], Sub);
  xor xor_2 (xor_1_out[1], in_5[1], Sub);
  xor xor_3 (xor_1_out[2], in_5[2], Sub);
  xor xor_4 (xor_1_out[3], in_5[3], Sub);
  xor xor_5 (xor_1_out[4], B, Sub);
  Adder #(.width(5)) adder_1 (.a({in_2, A}), .b(xor_1_out), .out({out_6, out_7}), .cin(Sub));  // open: cout
  and and_1 (and_1_out, B, in_2);
  not not_1 (not_1_out, out_6);
  not not_2 (not_2_out, B);
  and and_2 (and_2_out, not_2_out, not_3_out);
  not not_3 (not_3_out, in_2);
  not not_4 (not_4_out, B);
  and and_3 (and_3_out, in_2, not_4_out, Sub);
  not not_5 (not_5_out, out_6);
  not not_6 (not_6_out, in_2);
  and and_4 (and_4_out, not_6_out, B, out_6);
  and and_5 (and_5_out, and_1_out, not_1_out);
  and and_6 (and_6_out, and_2_out, out_6);
  and and_7 (and_7_out, and_3_out, not_5_out);
  and and_8 (and_8_out, and_4_out, Sub);
  or or_1 (Overflow, and_5_out, and_6_out, and_7_out, and_8_out);

  // Notes on the sheet:
  //   Controlled Adder/Subtracter with Overflow
  //   A
  //   Out
  //   Out
  //   B
  //   Sub
  //   (AB) * ~Out
  //   (~A*~B) * Out
  //   A*~B*~Out*Sub
  //   ~A*B*Out*Sub
endmodule
