// Logisim project lab9.circ as structural Verilog: 1 circuit, main circuit main
module main (
  output [7:0] Output_Display,
  output PC,
  output Inc,
  output Amux,
  output Mar,
  output Mst,
  output Ir,
  output Demux,
  output Acc,
  output Out,
  output Sub
);

  wire Add_out, and_1_out, and_2_out, and_3_out, and_6_out, and_7_out, and_11_out, and_13_out, clock_1_out,
       CLR_out, decoder_1_out2, decoder_1_out3, Hlt_out, Jaz_out, Jmp_out, Lda_out, not_1_out, not_2_out,
       or_3_out, or_4_out, Out_out, Sta_out, Sub_out;
  wire [1:0] RT_State_q;
  wire [3:0] counter_1_q, multiplexer_1_out, not_3_out, register_1_q;
  wire [7:0] adder_1_out, multiplexer_2_out, not_4_out, ram_1_data, register_2_q, register_3_q, xor_1_out;

  Button CLR (.out(CLR_out));
  and and_1 (and_1_out, clock_1_out, not_2_out);
  Clock clock_1 (.out(clock_1_out));
  Counter #(.width(4), .max('hf)) counter_1 (
    .load(PC), .D(register_2_q[3:0]), .count(Inc), .Q(counter_1_q), .clk(and_1_out), .clr(CLR_out));  // open: carry
  or or_1 (PC, and_2_out, and_3_out);
  and and_2 (and_2_out, decoder_1_out2, Jmp_out);
  and and_3 (and_3_out, decoder_1_out2, and_11_out);
  not not_1 (not_1_out, and_1_out);
  Multiplexer #(.width(4), .enable("false")) multiplexer_1 (
    .in0(counter_1_q), .in1(register_2_q[3:0]), .out(multiplexer_1_out), .sel(Amux));
  or or_2 (Mar, Inc, and_6_out);
  and and_4 (Amux, decoder_1_out2, or_3_out);
  Decoder #(.select(2), .enable("false")) decoder_1 (
    .out0(Inc), .out1(Ir), .out2(decoder_1_out2), .out3(decoder_1_out3), .sel(RT_State_q));
  Counter #(.width(2), .max('h3)) RT_State (
    .Q(RT_State_q), .clk(not_1_out), .clr(CLR_out));  // open: load, D, count, carry
  Register #(.width(4)) register_1 (.D(multiplexer_1_out), .en(Mar), .Q(register_1_q), .clk(and_1_out), .clr(CLR_out));
  and and_5 (Mst, decoder_1_out3, Sta_out);
  or or_3 (or_3_out, or_4_out, Sta_out);
  and and_6 (and_6_out, decoder_1_out2, or_3_out);
  and and_7 (and_7_out, decoder_1_out2, Hlt_out);
  not not_2 (not_2_out, and_7_out);
  RAM #(.addrWidth(4), .bus("separate")) ram_1 (
    .addr(register_1_q), .din(register_3_q), .data(ram_1_data), .str(Mst), .clk(and_1_out));  // open: sel, ld, clr
  and and_8 (Demux, decoder_1_out3, Lda_out);
  or or_4 (or_4_out, Lda_out, Add_out, Sub_out);
  Multiplexer #(.width(8), .enable("false")) multiplexer_2 (
    .in0(adder_1_out), .in1(ram_1_data), .out(multiplexer_2_out), .sel(Demux));
  Register register_2 (.D(ram_1_data), .en(Ir), .Q(register_2_q), .clk(and_1_out), .clr(CLR_out));
  and and_9 (Acc, decoder_1_out3, or_4_out);
  Register register_3 (.D(multiplexer_2_out), .en(Acc), .Q(register_3_q), .clk(and_1_out), .clr(CLR_out));
  and and_10 (Out, decoder_1_out2, Out_out);
  and and_11 (and_11_out, Jaz_out, and_13_out);
  Register register_4 (.D(register_3_q), .en(Out), .Q(Output_Display), .clk(and_1_out), .clr(CLR_out));
  assign xor_1_out = ram_1_data ^ {8{Sub}};  // XOR_Gate xor_1, 8 bits wide
  and and_12 (Sub, decoder_1_out3, Sub_out);
  and Lda (Lda_out, not_3_out[3], not_3_out[2], not_3_out[1], not_3_out[0]);
  and Add (Add_out, not_3_out[3], not_3_out[2], not_3_out[1], register_2_q[4]);
  and u_Sub (Sub_out, not_3_out[3], not_3_out[2], register_2_q[5], not_3_out[0]);
  and Sta (Sta_out, not_3_out[3], not_3_out[2], register_2_q[5], register_2_q[4]);
  and Jmp (Jmp_out, not_3_out[3], register_2_q[6], not_3_out[1], not_3_out[0]);
  and Jaz (Jaz_out, not_3_out[3], register_2_q[6], not_3_out[1], register_2_q[4]);
  and u_Out (Out_out, register_2_q[7], register_2_q[6], register_2_q[5], not_3_out[0]);
  and Hlt (Hlt_out, register_2_q[7], register_2_q[6], register_2_q[5], register_2_q[4]);
  Adder adder_1 (.a(register_3_q), .b(xor_1_out), .out(adder_1_out), .cin(Sub));  // open: cout
  assign not_3_out = ~register_2_q[7:4];  // NOT_Gate not_3, 4 bits wide
  assign not_4_out = ~register_3_q;  // NOT_Gate not_4, 8 bits wide
  and and_13 (and_13_out, not_4_out[7], not_4_out[6], not_4_out[5], not_4_out[4], not_4_out[3], not_4_out[2], not_4_out[1], not_4_out[0]);

  // Notes on the sheet:
  //   PC
  //   t3
  //   t2
  //   t1
  //   RT State
  //   t4
  //   MAR
  //   16B RAM
  //   t3 ^ Hlt
  //   LDA V ADD V SUB
  //   LDA V ADD V SUB V STA
  //   JMP V JAZ
  //   IR
  //   Out
  //   ACC
endmodule
